# Fritzing sketch rotary_encoder (saved by Fritzing 0.9.3b)

parts:
  ENCODER1 = Rotary Encoder with Knob
  Raspberry_Pi_Zero1 = Raspberry Pi Zero

nets:
  N1: ENCODER1.no_name_yet#1, ENCODER1.no_name_yet#2, Raspberry_Pi_Zero1.GPIO9, Raspberry_Pi_Zero1.GND, Raspberry_Pi_Zero1.GPIO24
  N2: ENCODER1.no_name_yet#3, Raspberry_Pi_Zero1.GPIO25
  N3: ENCODER1.no_name_yet#4, Raspberry_Pi_Zero1.GPIO23
  N4: ENCODER1.no_name_yet#5, Raspberry_Pi_Zero1.3v3

custom parts:
  Rotary Encoder with Knob: Rotary Encoder with 1/4" Shaft and Knob
